# Fritzing sketch sensornode (saved by Fritzing 0.7.12b)
breadboards: 1

parts:
  Arduino1 = Arduino
  U1 = XBee
  RHT1 = Humidity and Temperature Sensor RHT03
  R1 = Resistor [tolerance=±5% resistance=220 package=THT]
  ZX-SOUND1 = ZX-SOUND

nets:
  GND: Arduino1.GND, U1.GND, ZX-SOUND1.GND
  N1: Arduino1.D11, RHT1.Data-signal, R1.Pin_1
  N2: Arduino1.D1TX, U1.pin3
  N3: Arduino1.D0RX, U1.pin2
  VCC: Arduino1.3V3, U1.VCC, RHT1.Vcc, R1.Pin_0, ZX-SOUND1.VCC
  N4: Arduino1.A5, ZX-SOUND1.SGN

custom parts:
  ZX-SOUND: Sound detection module Detects sound pressure with Condenser Microphone. Output voltage 0 to +5V varies from sound pressure level that microphone detected. If more pressure is applied, the output voltage goes high and vice versa.
