# Fritzing sketch serverside (saved by Fritzing 0.7.12b)

parts:
  Raspberry_Pi1 = Raspberry Pi (Model B)  # not connected
  Part1 = XBee Explorer Regulated
  CONN1 = USB connector [package=THT]

nets:
  GND: Part1.GND, CONN1.GND, CONN1.chassis5, CONN1.chassis6
  N1: Part1.DIN, CONN1.d-
  N2: Part1.DOUT, CONN1.d+
  5V: Part1.5V, CONN1.5V

custom parts:
  Raspberry Pi (Model B): Raspberry Pi Single-board Computer, Model B
